# Fritzing sketch Digital_Pot_Control (saved by Fritzing 1.0.2b)
breadboards: 1

parts:
  A1 = Raspberry Pi Pico W
  A2 = X9C103S module
  LED1 = smd LED [color="Red (633nm)" package="0603 [SMD]"]

nets:
  N1: A1.pin_3, A1.pin_8, A1.pin_13, A1.pin_18, A1.pin_23, A1.pin_28, A1.pin_33, A1.pin_38, A1.pin_42, A2.Pin_5, A2.Pin_8, LED1.anode
  N2: A1.pin_17, A2.Pin_2
  N3: A1.pin_19, A2.Pin_3
  N4: A1.pin_20, A2.Pin_4
  N5: A1.pin_36, A2.Pin_1, A2.Pin_6
  N6: A2.Pin_7, LED1.cathode

custom parts:
  Raspberry Pi Pico W: Raspberry Pi Pico W. Based around the RP2040 microcontroller the Pico W is a low cost microcontroller device bringing Raspberry Pi quality, cost, and easy of use to the microcontroller space. The areas marked KEEPOUT in pcb silkscreen should not have traces running through them to avoid shorts on a soldered in module!
  X9C103S module: Digital Potentiometer Module X9C103S Voltage Regulator Electronic For Arduino .
